# Fritzing sketch LedPcb (saved by Fritzing 0.9.3b)
circuit board: 5.15596cm x 4.53316cm
circuit board: 5.74722cm x 4.59055cm
breadboards: 1

parts:
  J10 = shrouded pin header, 10 pins [form="♂ (shrouded male)"]
  J11 = shrouded pin header, 10 pins [form="♂ (shrouded male)"]
  J12 = female pin header, 3 pins [form="♀ (female)"]
  J13 = female pin header, 3 pins [form="♀ (female)"]
  J15 = shrouded pin header, 10 pins [form="♂ (shrouded male)"]
  J16 = female pin header, 3 pins [form="♀ (female)"]
  J17 = female pin header, 3 pins [form="♀ (female)"]
  J14 = shrouded pin header, 10 pins [form="♂ (shrouded male)"]

nets:
  N1: J10.pin1, J11.pin5, J12.pin2
  N2: J10.pin3, J11.pin3, J12.pin3
  N3: J10.pin4, J11.pin4, J12.pin1
  N4: J10.pin8, J11.pin8, J13.pin1
  N5: J10.pin9, J11.pin7, J13.pin2
  N6: J10.pin10, J11.pin6, J13.pin3
  N7: J15.pin3, J16.pin3, J14.pin3
  N8: J15.pin4, J16.pin1, J14.pin2
  N9: J15.pin5, J16.pin2, J14.pin1
  N10: J15.pin6, J17.pin3, J14.pin10
  N11: J15.pin7, J17.pin2, J14.pin9
  N12: J15.pin8, J17.pin1, J14.pin8

notes:
  B
  G
  R
  -
  +
